# Fritzing sketch OpenSpool-AMS (saved by Fritzing 1.0.4)

parts:
  Part1 = PN532 Elechouse RFID NFC Module V3
  Part2 = PN532 Elechouse RFID NFC Module V3
  Part3 = PN532 Elechouse RFID NFC Module V3
  Part4 = PN532 Elechouse RFID NFC Module V3
  Part5 = PN532 Elechouse RFID NFC Module V3  # not connected
  Part6 = PN532 Elechouse RFID NFC Module V3  # not connected
  Part7 = PN532 Elechouse RFID NFC Module V3  # not connected
  Part8 = PN532 Elechouse RFID NFC Module V3  # not connected
  Part9 = PN532 Elechouse RFID NFC Module V3  # not connected
  U2 = WS2812 RGB LED strip
  A1 = ESP32-S3-WROOM-1-N16R8 dev board

nets:
  N1: Part1.SCK, A1.Pin_18
  N2: Part1.MISO, A1.Pin_19
  N3: Part1.MOSI, A1.Pin_17
  N4: Part1.SS, A1.Pin_4
  N5: Part1.VCC, A1.Pin_1
  N6: Part1.GND, A1.Pin_23, A1.Pin_44
  N7: Part2.SS, A1.Pin_5
  N8: Part3.SS, A1.Pin_6
  N9: Part4.SS, A1.Pin_7
  N10: U2.DIN, A1.Pin_27

custom parts:
  PN532 Elechouse RFID NFC Module V3: NFC is a popular technology in recent years. We often heard this work while smart phone company such as Samsung or HTC introduces their latest high-end phones. Almost all the high-end phone in the market support NFC. Near field communication (NFC) is a set of standards for smart phones and similar devices to establish radio communication with each other by touching them together or bringing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
  WS2812 RGB LED strip: WS2812 strip
  ESP32-S3-WROOM-1-N16R8 dev board: ESP32-S3 WIFI+BLE5.0 Development Board ESP32-S3-WROOM-1-N16R8(16M Flash/8SRAM).
