# Fritzing sketch OpenSpool-Mini (saved by Fritzing 1.0.4)

parts:
  Part5 = PN532 Elechouse RFID NFC Module V3
  A2 = Wemos S2 Mini [part_number="WeMos D1 Mini Lite"]
  U2 = WS2812 RGB LED strip
  Part6 = I2C level shifter bidirectional
  J2 = Wago 221-415
  J4 = Wago 221-415

nets:
  N1: Part5.SCK, A2.Pin_30
  N2: Part5.MISO, A2.Pin_23
  N3: Part5.MOSI, A2.Pin_22
  N4: Part5.SS, A2.Pin_29
  VCC: Part5.VCC, A2.Pin_17, U2.VCC, Part6.HV, J2.Pin_1, J2.Pin_2, J2.Pin_3, J2.Pin_4, J2.Pin_5
  GND: Part5.GND, A2.Pin_26, U2.GND, Part6.GND, J4.Pin_1, J4.Pin_2, J4.Pin_3, J4.Pin_4, J4.Pin_5
  N5: A2.Pin_8, Part6.LV
  N6: A2.Pin_19, Part6.LV1
  N7: U2.DIN, Part6.HV1

custom parts:
  PN532 Elechouse RFID NFC Module V3: NFC is a popular technology in recent years. We often heard this work while smart phone company such as Samsung or HTC introduces their latest high-end phones. Almost all the high-end phone in the market support NFC. Near field communication (NFC) is a set of standards for smart phones and similar devices to establish radio communication with each other by touching them together or bringing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
  Wemos S2 Mini: A mini wifi board based on the ESP32-S2FN4R2.
  WS2812 RGB LED strip: WS2812 strip
  Wago 221-415: Wago 221-415 5 position splicing connector 12AWG.
