# Fritzing sketch OpenSpool (saved by Fritzing 1.0.4)

parts:
  Part1 = PN532 Elechouse RFID NFC Module V3
  A1 = Wemos S2 Mini [part_number="WeMos D1 Mini Lite"]
  Part2 = PN532 Elechouse RFID NFC Module V3
  Part3 = PN532 Elechouse RFID NFC Module V3
  Part4 = PN532 Elechouse RFID NFC Module V3  # not connected
  Part5 = PN532 Elechouse RFID NFC Module V3  # not connected
  Part6 = PN532 Elechouse RFID NFC Module V3  # not connected
  Part7 = PN532 Elechouse RFID NFC Module V3  # not connected

nets:
  N1: Part1.SCK, A1.Pin_30, Part2.SCK, Part3.SCK
  N2: Part1.MISO, A1.Pin_23, Part2.MISO, Part3.MISO
  N3: Part1.MOSI, A1.Pin_22, Part2.MOSI, Part3.MOSI
  N4: Part1.SS, A1.Pin_29
  VCC: Part1.VCC, A1.Pin_17, Part2.VCC, Part3.VCC
  GND: Part1.GND, A1.Pin_18, A1.Pin_26, Part2.GND, Part3.GND
  N5: A1.Pin_27, Part2.SS
  N6: A1.Pin_28, Part3.SS

notes:
  External AMS
  AMS Slot 1

custom parts:
  PN532 Elechouse RFID NFC Module V3: NFC is a popular technology in recent years. We often heard this work while smart phone company such as Samsung or HTC introduces their latest high-end phones. Almost all the high-end phone in the market support NFC. Near field communication (NFC) is a set of standards for smart phones and similar devices to establish radio communication with each other by touching them together or bringing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
  Wemos S2 Mini: A mini wifi board based on the ESP32-S2FN4R2.
