# Fritzing sketch OpenSpool-Mini (saved by Fritzing 1.0.5)

parts:
  Part5 = PN532 Elechouse RFID NFC Module V3
  A2 = Wemos S2 Mini [part_number="WeMos D1 Mini Lite"]
  Part6 = I2C level shifter bidirectional
  LED1 = WS2812B RGB LED

nets:
  N1: Part5.SCK, A2.Pin_30
  N2: Part5.MISO, A2.Pin_23
  N3: Part5.MOSI, A2.Pin_22
  N4: Part5.SS, A2.Pin_29
  N5: Part5.VCC, A2.Pin_17, Part6.HV, LED1.pin2
  GND: Part5.GND, A2.Pin_18, A2.Pin_26, Part6.GND, LED1.pin1
  N6: A2.Pin_8, Part6.LV
  N7: A2.Pin_19, Part6.LV1
  N8: Part6.HV1, LED1.pin3

custom parts:
  PN532 Elechouse RFID NFC Module V3: NFC is a popular technology in recent years. We often heard this work while smart phone company such as Samsung or HTC introduces their latest high-end phones. Almost all the high-end phone in the market support NFC. Near field communication (NFC) is a set of standards for smart phones and similar devices to establish radio communication with each other by touching them together or bringing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
  Wemos S2 Mini: A mini wifi board based on the ESP32-S2FN4R2.
  WS2812B RGB LED: A single addressable RGB LED
